// Logisim project 1rs.circ as structural Verilog: 1 circuit, main circuit main
module main (
  input  S,
  input  R,
  output Q,
  output NQ
);

  nand nand_1 (Q, S, NQ);
  nand nand_2 (NQ, Q, R);
endmodule
