// Logisim project 2d.circ as structural Verilog: 1 circuit, main circuit main
module main (
  input  in_1,
  output out_2,
  output out_3
);

  wire clock_1_out;

  D_Flip_Flop d_ff_1 (.D(in_1), .clk(clock_1_out), .Q(out_2), .Qn(out_3));  // open: preset, reset
  Clock clock_1 (.out(clock_1_out));
endmodule
