// Logisim project 3jk.circ as structural Verilog: 1 circuit, main circuit main
module main (
  input  in_1,
  input  in_2,
  output out_3,
  output out_4
);

  wire clock_1_out;

  Clock clock_1 (.out(clock_1_out));
  J_K_Flip_Flop j_k_ff_1 (.J(in_1), .K(in_2), .clk(clock_1_out), .Q(out_3), .Qn(out_4));  // open: preset, reset
endmodule
