// Logisim project 6tjk.circ as structural Verilog: 1 circuit, main circuit main
module main (
  input  in_1,
  output out_2,
  output out_3
);

  wire clock_1_out;

  Clock clock_1 (.out(clock_1_out));
  J_K_Flip_Flop j_k_ff_1 (.J(in_1), .K(in_1), .clk(clock_1_out), .Q(out_2), .Qn(out_3));  // open: preset, reset
endmodule
